# Fritzing sketch Digital_Notebook_Sketch (saved by Fritzing 1.0.6)
breadboards: 1

parts:
  A3 = Micro SD card reader
  OLED_I2C6 = OLED 128x64 I2C Monochrome Display  # not connected
  X2 = USB Connectors [package=usb-microb]
  A5 = XIAO ESP32C3-tht

nets:
  N1: A3.Pin_1, A5.Pin_20
  N2: A3.Pin_2, A5.Pin_12
  N3: A3.Pin_3, A5.Pin_19
  N4: A3.Pin_4, A5.Pin_17
  N5: A3.Pin_5, A5.Pin_18
  N6: A3.Pin_6, X2.GND, A5.Pin_21
  N7: X2.VBUS, A5.Pin_22

custom parts:
  Micro SD card reader: Micro SD card reader.
  USB Connectors: USB Connectors USB-B-PTH is fully proven SKU : PRT-00139 USB-miniB is fully proven SKU : PRT-00587 USB-A-PCB is untested. USB-A-H is throughly reviewed, but untested. Spark Fun Electronics SKU : PRT-00437 USB-B-SMT is throughly reviewed, but untested. Needs silkscreen touching up. USB-A-S has not been used/tested USB-MB-H has not been used/tested
  XIAO ESP32C3-tht: Seeed Studio XIAO ESP32C3 adopts new RISC-V architecture, supporting both Wi-Fi and BLE wireless connectivities.
